# Fritzing sketch sketch (saved by Fritzing 0.8.7b)
breadboards: 1

parts:
  LED1 = RGB LED (com. anode, rbg) [package="5 mm [THT]"]
  U1 = NodeMCU V1.0
  DHT1 = DHT11 Humitidy and Temperature Sensor

nets:
  N1: LED1.red_cathode, U1.D1
  3V3: LED1.common_anode, U1.3V3, DHT1.VDD
  N2: LED1.blue_cathode, U1.D2
  N3: LED1.green_cathode, U1.D3
  N4: U1.D4, DHT1.DATA
  GND: U1.GND, DHT1.GND

custom parts:
  NodeMCU V1.0: ESP8266 based NodeMCU
  DHT11 Humitidy and Temperature Sensor: DHT11 Humidity and Temperature Sensor
